// Digital circuit 4-Bit-GPR.dig as structural Verilog
module _4_Bit_GPR (
  input  Clock,
  input  [3:0] Input,
  input  [1:0] Clear_Store_Load,
  output [3:0] Output
);

  wire [3:0] multiplexer_1_out;

  Multiplexer #(.Bits(4), .Selector_Bits(2)) multiplexer_1 (
    .sel(Clear_Store_Load), .in_0(4'b0000), .in_1(Input), .in_2(Output), .in_3(4'b1111),
    .out(multiplexer_1_out));
  D_FF d_ff_1 (.D(multiplexer_1_out[3]), .C(Clock), .Q(Output[3]));  // open: nQ
  D_FF d_ff_2 (.D(multiplexer_1_out[2]), .C(Clock), .Q(Output[2]));  // open: nQ
  D_FF d_ff_3 (.D(multiplexer_1_out[1]), .C(Clock), .Q(Output[1]));  // open: nQ
  D_FF d_ff_4 (.D(multiplexer_1_out[0]), .C(Clock), .Q(Output[0]));  // open: nQ
endmodule
